// Logisim project Lab_6.circ as structural Verilog: 18 circuits, main circuit main
module main (
  input  Input_2,
  input  Input_1
);

  wire b0, b1, b2, b3, b4, b5, b6, c0, c1, c2, c3, c4, c5, c6, clock_1_out, not_1_out;
  wire [3:0] just_one_decoder_1_output_bus_1;
  wire [7:7] Bin2Hex_1_hex0, Bin2Hex_1_hex1;

  Clock clock_1 (.out(clock_1_out));
  not not_1 (not_1_out, Input_2);
  just_one_decoder just_one_decoder_1 (
    .reset(not_1_out), .en(Input_1), .CLK(clock_1_out), .Output_bus_1(just_one_decoder_1_output_bus_1));
  _7_Segment_Display #(.active("false")) L_7_Segment_Display_3 (
    .g(b6), .f(b5), .a(b0), .b(b1), .e(b4), .d(b3), .c(b2), .dp(1'b1));
  _7_Segment_Display #(.active("false")) L_7_Segment_Display_4 (
    .g(c6), .f(c5), .a(c0), .b(c1), .e(c4), .d(c3), .c(c2), .dp(1'b1));
  Bin2Hex Bin2Hex_1 (
    .v3(just_one_decoder_1_output_bus_1[3]), .v2(just_one_decoder_1_output_bus_1[2]),
    .v1(just_one_decoder_1_output_bus_1[1]), .v0(just_one_decoder_1_output_bus_1[0]),
    .HEX1({Bin2Hex_1_hex1[7], b6, b5, b4, b3, b2, b1, b0}),
    .HEX0({Bin2Hex_1_hex0[7], c6, c5, c4, c3, c2, c1, c0}));

  // Notes on the sheet:
  //   Counter Display
endmodule

module Seg7_Decoder (
  input  i_m3,
  input  i_m2,
  input  i_m1,
  input  i_m0,
  output [7:0] o_seg
);

  wire and_1_out, and_2_out, and_3_out, and_4_out, and_5_out, and_6_out, and_7_out, and_8_out, and_9_out,
       and_10_out, and_11_out, and_12_out, and_13_out, and_14_out, and_15_out, and_16_out, and_17_out,
       and_18_out, and_19_out, and_20_out, and_21_out, and_22_out, and_23_out, not_1_out, not_2_out,
       not_3_out, not_4_out;

  not not_1 (not_1_out, i_m3);
  not not_2 (not_2_out, i_m2);
  not not_3 (not_3_out, i_m1);
  not not_4 (not_4_out, i_m0);
  and and_1 (and_1_out, not_1_out, not_2_out, not_3_out);
  and and_2 (and_2_out, not_1_out, i_m2, i_m1, i_m0);
  and and_3 (and_3_out, i_m3, not_2_out, i_m1);
  and and_4 (and_4_out, not_1_out, not_2_out, i_m0);
  and and_5 (and_5_out, not_1_out, not_2_out, i_m1);
  and and_6 (and_6_out, not_2_out, i_m1, i_m0);
  and and_7 (and_7_out, i_m3, i_m2, not_3_out);
  and and_8 (and_8_out, not_1_out, i_m2, not_3_out);
  and and_9 (and_9_out, i_m3, i_m2, i_m1);
  and and_10 (and_10_out, not_1_out, not_2_out, not_3_out, i_m0);
  and and_11 (and_11_out, not_1_out, i_m2, not_3_out, not_4_out);
  and and_12 (and_12_out, not_1_out, i_m2, i_m1, i_m0);
  and and_13 (and_13_out, i_m3, not_2_out, i_m1, i_m0);
  and and_14 (and_14_out, i_m3, i_m2, i_m1, not_4_out);
  and and_15 (and_15_out, not_1_out, not_2_out, i_m1, not_4_out);
  and and_16 (and_16_out, i_m3, i_m2, not_3_out, not_4_out);
  and and_17 (and_17_out, not_1_out, i_m2, not_3_out, i_m0);
  and and_18 (and_18_out, not_1_out, i_m2, i_m1, not_4_out);
  and and_19 (and_19_out, i_m3, i_m2, i_m1, i_m0);
  and and_20 (and_20_out, not_1_out, not_2_out, not_3_out, i_m0);
  and and_21 (and_21_out, not_1_out, i_m2, not_3_out, not_4_out);
  and and_22 (and_22_out, i_m3, not_2_out, i_m1, i_m0);
  and and_23 (and_23_out, i_m3, i_m2, i_m1, not_4_out);
  or or_1 (o_seg[6], and_1_out, and_2_out, and_3_out);
  or or_2 (o_seg[5], and_4_out, and_5_out, and_6_out, and_7_out);
  or or_3 (o_seg[4], i_m0, and_8_out, and_9_out);
  or or_4 (o_seg[3], and_10_out, and_11_out, and_12_out, and_13_out, and_14_out);
  or or_5 (o_seg[2], and_15_out, and_16_out);
  or or_6 (o_seg[1], and_17_out, and_18_out, and_19_out);
  or or_7 (o_seg[0], and_20_out, and_21_out, and_22_out, and_23_out);

  assign o_seg[7] = 1'b1;
endmodule

module CircuitA (
  input  i2,
  input  i1,
  input  i0,
  output o2,
  output o1,
  output o0
);

  not not_1 (o1, i1);
  and and_1 (o2, i2, i1);

  assign o0 = i0;
endmodule

module myComparator (
  input  v3,
  input  v2,
  input  v1,
  input  v0,
  output z
);

  wire and_1_out, and_2_out;

  and and_1 (and_1_out, v3, v1);
  and and_2 (and_2_out, v3, v2);
  or or_1 (z, and_1_out, and_2_out);
endmodule

module CircuitB (
  input  z,
  output s6,
  output s5,
  output s4,
  output s3,
  output s2,
  output s1,
  output s0
);


  assign s0 = z;
  assign s1 = 1'b0;
  assign s2 = 1'b0;
  assign s3 = z;
  assign s4 = z;
  assign s5 = z;
  assign s6 = 1'b1;
endmodule

module Bin2Hex (
  input  v3,
  input  v2,
  input  v1,
  input  v0,
  output [7:0] HEX1,
  output [7:0] HEX0
);

  wire z;

  myComparator myComparator_1 (.v3(v3), .v2(v2), .v1(v1), .v0(v0), .z(z));
  CircuitB CircuitB_1 (
    .z(z), .s6(HEX1[6]), .s5(HEX1[5]), .s4(HEX1[4]), .s3(HEX1[3]), .s2(HEX1[2]), .s1(HEX1[1]), .s0(HEX1[0]));
  Seg7_Decoder Seg7_Decoder_1 (.i_m3(v3), .i_m2(v2), .i_m1(v1), .i_m0(v0), .o_seg(HEX0));

  assign HEX1[7] = 1'b1;
endmodule

module UpCounter_Template (
  input  en,
  input  CLK,
  output [3:0] Q_2
);

  wire t_ff_1_qn, t_ff_2_qn, t_ff_3_qn;

  T_Flip_Flop t_ff_1 (.T(en), .clk(CLK), .Q(Q_2[0]), .Qn(t_ff_1_qn));  // open: reset, preset
  T_Flip_Flop t_ff_2 (.T(en), .clk(t_ff_1_qn), .Q(Q_2[1]), .Qn(t_ff_2_qn));  // open: reset, preset
  T_Flip_Flop t_ff_3 (.T(en), .clk(t_ff_2_qn), .Q(Q_2[2]), .Qn(t_ff_3_qn));  // open: reset, preset
  T_Flip_Flop t_ff_4 (.T(en), .clk(t_ff_3_qn), .Q(Q_2[3]));  // open: Qn, reset, preset
endmodule

module DownCounter_Template (
  input  en,
  input  CLK,
  output [3:0] out_3
);

  T_Flip_Flop t_ff_1 (.T(en), .clk(CLK), .Q(out_3[0]));  // open: Qn, reset, preset
  T_Flip_Flop t_ff_2 (.T(en), .clk(out_3[0]), .Q(out_3[1]));  // open: Qn, reset, preset
  T_Flip_Flop t_ff_3 (.T(en), .clk(out_3[1]), .Q(out_3[2]));  // open: Qn, reset, preset
  T_Flip_Flop t_ff_4 (.T(en), .clk(out_3[2]), .Q(out_3[3]));  // open: Qn, reset, preset
endmodule

module Mod5_Template (
  input  in_1,
  input  in_2,
  input  in_3,
  input  in_4,
  output [3:0] out_5,
  output [3:0] out_6
);

  wire and_1_out, and_2_out, nand_1_out, nand_2_out, not_1_out, not_2_out, not_3_out, not_4_out, not_5_out,
       not_6_out, not_7_out, not_8_out, undriven;

  T_Flip_Flop t_ff_1 (.T(in_1), .clk(in_2), .Q(out_5[0]), .reset(not_1_out));  // open: Qn, preset
  not not_1 (not_1_out, nand_1_out);
  T_Flip_Flop t_ff_2 (.T(in_3), .clk(in_4), .Q(out_6[0]), .reset(not_2_out));  // open: Qn, preset
  not not_2 (not_2_out, nand_2_out);
  T_Flip_Flop t_ff_3 (.T(out_5[0]), .clk(in_2), .Q(out_5[1]), .reset(not_3_out));  // open: Qn, preset
  not not_3 (not_3_out, nand_1_out);
  T_Flip_Flop t_ff_4 (.T(out_6[0]), .clk(in_4), .Q(out_6[1]), .reset(not_4_out));  // open: Qn, preset
  not not_4 (not_4_out, nand_2_out);
  T_Flip_Flop t_ff_5 (.T(out_5[1]), .clk(in_2), .Q(out_5[2]), .reset(not_5_out));  // open: Qn, preset
  not not_5 (not_5_out, nand_1_out);
  and and_1 (and_1_out, out_6[0], out_6[1]);
  and and_2 (and_2_out, out_5[0], out_5[2]);
  T_Flip_Flop t_ff_6 (.T(and_1_out), .clk(in_4), .Q(out_6[2]), .reset(not_6_out));  // open: Qn, preset
  not not_6 (not_6_out, nand_2_out);
  T_Flip_Flop t_ff_7 (.T(and_2_out), .clk(in_2), .Q(out_5[3]), .reset(not_7_out));  // open: Qn, preset
  not not_7 (not_7_out, nand_1_out);
  T_Flip_Flop t_ff_8 (.T(out_6[2]), .clk(in_4), .Q(out_6[3]), .reset(not_8_out));  // open: Qn, preset
  not not_8 (not_8_out, nand_2_out);
  nand nand_1 (nand_1_out, out_5[0], in_1, out_5[3]);
  nand nand_2 (nand_2_out, out_6[0], out_6[2], undriven);
endmodule

module Johnson_Counter_Template (
  input  Reset,
  input  CLK,
  output [3:0] out_3
);

  wire d_ff_4_qn;

  D_Flip_Flop d_ff_1 (.D(d_ff_4_qn), .clk(CLK), .Q(out_3[0]), .reset(Reset));  // open: Qn, preset
  D_Flip_Flop d_ff_2 (.D(out_3[0]), .clk(CLK), .Q(out_3[1]), .reset(Reset));  // open: Qn, preset
  D_Flip_Flop d_ff_3 (.D(out_3[1]), .clk(CLK), .Q(out_3[2]), .reset(Reset));  // open: Qn, preset
  D_Flip_Flop d_ff_4 (.D(out_3[2]), .clk(CLK), .Q(out_3[3]), .Qn(d_ff_4_qn), .reset(Reset));  // open: preset
endmodule

module down_with_reset (
  input  en,
  input  CLK,
  input  in_3,
  output [3:0] out_4
);

  wire not_1_out, not_2_out, not_3_out, not_4_out;

  T_Flip_Flop t_ff_1 (.T(en), .clk(CLK), .Q(out_4[0]), .reset(not_1_out));  // open: Qn, preset
  not not_1 (not_1_out, in_3);
  T_Flip_Flop t_ff_2 (.T(en), .clk(out_4[0]), .Q(out_4[1]), .reset(not_2_out));  // open: Qn, preset
  not not_2 (not_2_out, in_3);
  T_Flip_Flop t_ff_3 (.T(en), .clk(out_4[1]), .Q(out_4[2]), .reset(not_3_out));  // open: Qn, preset
  not not_3 (not_3_out, in_3);
  T_Flip_Flop t_ff_4 (.T(en), .clk(out_4[2]), .Q(out_4[3]), .reset(not_4_out));  // open: Qn, preset
  not not_4 (not_4_out, in_3);
endmodule

module mod_10 (
  input  reset,
  input  en,
  input  CLK,
  output [3:0] out_4
);

  wire nand_1_out, not_1_out, not_2_out, not_3_out, not_4_out, not_5_out, not_6_out, not_7_out, not_8_out,
       or_1_out;

  T_Flip_Flop t_ff_1 (.T(en), .clk(not_1_out), .Q(out_4[0]), .reset(not_2_out));  // open: Qn, preset
  not not_1 (not_1_out, CLK);
  not not_2 (not_2_out, or_1_out);
  T_Flip_Flop t_ff_2 (.T(en), .clk(not_3_out), .Q(out_4[1]), .reset(not_4_out));  // open: Qn, preset
  not not_3 (not_3_out, out_4[0]);
  not not_4 (not_4_out, or_1_out);
  T_Flip_Flop t_ff_3 (.T(en), .clk(not_5_out), .Q(out_4[2]), .reset(not_6_out));  // open: Qn, preset
  not not_5 (not_5_out, out_4[1]);
  not not_6 (not_6_out, or_1_out);
  T_Flip_Flop t_ff_4 (.T(en), .clk(not_7_out), .Q(out_4[3]), .reset(not_8_out));  // open: Qn, preset
  not not_7 (not_7_out, out_4[2]);
  not not_8 (not_8_out, or_1_out);
  nand nand_1 (nand_1_out, out_4[1], out_4[3]);
  or or_1 (or_1_out, nand_1_out, reset);
endmodule

module Mod_10_countdown (
  input  in_1,
  input  in_2,
  input  in_3,
  output [3:0] out_4
);

  wire [3:0] down_with_reset_1_out_4, mod_10_1_out_4;

  mod_10 mod_10_1 (.reset(in_3), .en(in_1), .CLK(in_2), .out_4(mod_10_1_out_4));
  and and_1 (out_4[3], mod_10_1_out_4[3], down_with_reset_1_out_4[3]);
  and and_2 (out_4[2], mod_10_1_out_4[2], down_with_reset_1_out_4[2]);
  and and_3 (out_4[1], mod_10_1_out_4[1], down_with_reset_1_out_4[1]);
  and and_4 (out_4[0], mod_10_1_out_4[0], down_with_reset_1_out_4[0]);
  down_with_reset down_with_reset_1 (.en(in_1), .CLK(in_2), .in_3(in_3), .out_4(down_with_reset_1_out_4));
endmodule

module rando (
  input  reset,
  input  en,
  input  CLK,
  output [3:0] out_4
);

  wire and_1_out, and_2_out, and_3_out, and_4_out, and_5_out, and_6_out, and_7_out, and_8_out, and_9_out,
       and_10_out, and_11_out, and_12_out, and_13_out, and_14_out, and_15_out, and_16_out, and_17_out,
       and_18_out, not_1_out, not_2_out, not_3_out, not_4_out, not_5_out, not_6_out, not_7_out, or_1_out,
       t_ff_1_q, t_ff_2_q, t_ff_3_q, t_ff_4_q;

  T_Flip_Flop t_ff_1 (.T(en), .clk(CLK), .Q(t_ff_1_q), .reset(or_1_out));  // open: Qn, preset
  T_Flip_Flop t_ff_2 (.T(en), .clk(t_ff_1_q), .Q(t_ff_2_q), .reset(or_1_out));  // open: Qn, preset
  T_Flip_Flop t_ff_3 (.T(en), .clk(t_ff_2_q), .Q(t_ff_3_q), .reset(or_1_out));  // open: Qn, preset
  not not_1 (not_1_out, t_ff_1_q);
  not not_2 (not_2_out, t_ff_4_q);
  not not_3 (not_3_out, t_ff_3_q);
  not not_4 (not_4_out, t_ff_2_q);
  not not_5 (not_5_out, t_ff_1_q);
  not not_6 (not_6_out, t_ff_2_q);
  not not_7 (not_7_out, t_ff_4_q);
  T_Flip_Flop t_ff_4 (.T(en), .clk(t_ff_3_q), .Q(t_ff_4_q), .reset(or_1_out));  // open: Qn, preset
  and and_1 (and_1_out, not_1_out, not_6_out, t_ff_3_q, not_7_out);
  or or_1 (or_1_out, and_1_out, reset);
  and and_2 (and_2_out, not_2_out, not_3_out, t_ff_2_q, not_5_out);
  and and_3 (and_3_out, t_ff_4_q, t_ff_3_q, not_4_out, t_ff_1_q);
  and and_4 (and_4_out, t_ff_4_q, t_ff_3_q, t_ff_2_q, not_5_out);
  and and_5 (and_5_out, not_3_out, t_ff_2_q, t_ff_1_q);
  and and_6 (and_6_out, not_2_out, t_ff_3_q, not_4_out);
  and and_7 (and_7_out, t_ff_4_q, not_3_out, t_ff_1_q);
  and and_8 (and_8_out, t_ff_4_q, not_3_out, t_ff_2_q);
  and and_9 (and_9_out, t_ff_3_q, not_4_out, not_5_out);
  and and_10 (and_10_out, not_2_out, not_3_out, t_ff_1_q);
  and and_11 (and_11_out, t_ff_3_q, not_4_out, not_5_out);
  and and_12 (and_12_out, not_2_out, t_ff_2_q, t_ff_1_q);
  and and_13 (and_13_out, t_ff_4_q, not_4_out, not_5_out);
  and and_14 (and_14_out, not_3_out, t_ff_2_q, t_ff_1_q);
  and and_15 (and_15_out, not_2_out, not_3_out, t_ff_1_q);
  and and_16 (and_16_out, not_2_out, not_4_out, t_ff_1_q);
  and and_17 (and_17_out, t_ff_3_q, t_ff_2_q, not_5_out);
  and and_18 (and_18_out, t_ff_4_q, not_5_out);
  or or_2 (out_4[3], and_2_out, and_3_out, and_4_out);
  or or_3 (out_4[2], and_5_out, and_6_out, and_7_out, and_8_out, and_9_out);
  or or_4 (out_4[1], and_10_out, and_11_out, and_12_out, and_13_out, and_14_out);
  or or_5 (out_4[0], and_15_out, and_16_out, and_17_out, and_18_out);
endmodule

module ran_2 (
  input  reset,
  input  en,
  input  CLK,
  output [3:0] Output_bus_1
);

  wire and_1_out, and_2_out, and_3_out, and_4_out, and_5_out, and_6_out, and_7_out, and_8_out, and_9_out,
       and_10_out, and_11_out, and_12_out, and_13_out, and_14_out, and_15_out, and_16_out, and_17_out,
       and_18_out, not_1_out, not_2_out, not_3_out, not_4_out, not_5_out, not_6_out, or_5_out, t_ff_1_q,
       t_ff_2_q, t_ff_3_q, t_ff_4_q;

  T_Flip_Flop t_ff_1 (.T(en), .clk(CLK), .Q(t_ff_1_q), .reset(or_5_out));  // open: Qn, preset
  T_Flip_Flop t_ff_2 (.T(en), .clk(t_ff_1_q), .Q(t_ff_2_q), .reset(or_5_out));  // open: Qn, preset
  T_Flip_Flop t_ff_3 (.T(en), .clk(t_ff_2_q), .Q(t_ff_3_q), .reset(or_5_out));  // open: Qn, preset
  not not_1 (not_1_out, t_ff_4_q);
  not not_2 (not_2_out, t_ff_3_q);
  not not_3 (not_3_out, t_ff_2_q);
  not not_4 (not_4_out, t_ff_1_q);
  not not_5 (not_5_out, t_ff_2_q);
  not not_6 (not_6_out, t_ff_4_q);
  T_Flip_Flop t_ff_4 (.T(en), .clk(t_ff_3_q), .Q(t_ff_4_q), .reset(or_5_out));  // open: Qn, preset
  and and_1 (and_1_out, not_1_out, not_2_out, t_ff_2_q, not_4_out);
  and and_2 (and_2_out, t_ff_4_q, t_ff_3_q, not_3_out, t_ff_1_q);
  and and_3 (and_3_out, t_ff_4_q, t_ff_3_q, t_ff_2_q, not_4_out);
  and and_4 (and_4_out, not_2_out, t_ff_2_q, t_ff_1_q);
  and and_5 (and_5_out, not_1_out, t_ff_3_q, not_3_out);
  and and_6 (and_6_out, t_ff_4_q, not_2_out, t_ff_1_q);
  and and_7 (and_7_out, t_ff_4_q, not_2_out, t_ff_2_q);
  and and_8 (and_8_out, t_ff_3_q, not_3_out, not_4_out);
  and and_9 (and_9_out, not_1_out, not_2_out, t_ff_1_q);
  and and_10 (and_10_out, t_ff_3_q, not_3_out, not_4_out);
  and and_11 (and_11_out, not_1_out, t_ff_2_q, t_ff_1_q);
  and and_12 (and_12_out, t_ff_4_q, not_3_out, not_4_out);
  and and_13 (and_13_out, not_2_out, t_ff_2_q, t_ff_1_q);
  and and_14 (and_14_out, not_1_out, not_2_out, t_ff_1_q);
  and and_15 (and_15_out, not_1_out, not_3_out, t_ff_1_q);
  and and_16 (and_16_out, t_ff_3_q, t_ff_2_q, not_4_out);
  and and_17 (and_17_out, t_ff_4_q, not_4_out);
  and and_18 (and_18_out, t_ff_1_q, not_5_out, t_ff_3_q, not_6_out);
  or or_1 (Output_bus_1[3], and_1_out, and_2_out, and_3_out);
  or or_2 (Output_bus_1[2], and_4_out, and_5_out, and_6_out, and_7_out, and_8_out);
  or or_3 (Output_bus_1[1], and_9_out, and_10_out, and_11_out, and_12_out, and_13_out);
  or or_4 (Output_bus_1[0], and_14_out, and_15_out, and_16_out, and_17_out);
  or or_5 (or_5_out, and_18_out, reset);
endmodule

module ran_3 (
  input  reset,
  input  en,
  input  CLK,
  output [3:0] out_4
);

  wire and_1_out, and_2_out, and_3_out, and_4_out, and_5_out, and_6_out, and_7_out, and_8_out, and_9_out,
       and_10_out, and_11_out, and_12_out, and_13_out, and_14_out, and_15_out, and_16_out, and_17_out,
       not_1_out, not_2_out, not_3_out, not_4_out, not_5_out, not_6_out, or_5_out, t_ff_1_q, t_ff_2_q,
       t_ff_3_q, t_ff_4_q;

  T_Flip_Flop t_ff_1 (.T(en), .clk(CLK), .Q(t_ff_1_q), .reset(or_5_out));  // open: Qn, preset
  T_Flip_Flop t_ff_2 (.T(en), .clk(t_ff_1_q), .Q(t_ff_2_q), .reset(or_5_out));  // open: Qn, preset
  not not_1 (not_1_out, t_ff_4_q);
  not not_2 (not_2_out, t_ff_3_q);
  not not_3 (not_3_out, t_ff_2_q);
  not not_4 (not_4_out, t_ff_1_q);
  T_Flip_Flop t_ff_3 (.T(en), .clk(t_ff_2_q), .Q(t_ff_3_q), .reset(or_5_out));  // open: Qn, preset
  and and_1 (and_1_out, not_1_out, not_2_out, t_ff_2_q, not_4_out);
  and and_2 (and_2_out, t_ff_4_q, t_ff_3_q, t_ff_1_q);
  or or_1 (out_4[3], and_1_out, and_2_out, and_3_out);
  and and_3 (and_3_out, t_ff_4_q, t_ff_3_q, t_ff_2_q);
  and and_4 (and_4_out, not_2_out, t_ff_2_q, t_ff_1_q);
  and and_5 (and_5_out, not_1_out, t_ff_3_q, not_3_out);
  and and_6 (and_6_out, t_ff_4_q, not_2_out, t_ff_1_q);
  and and_7 (and_7_out, t_ff_4_q, not_2_out, t_ff_2_q);
  and and_8 (and_8_out, t_ff_3_q, not_3_out, not_4_out);
  and and_9 (and_9_out, not_1_out, not_2_out, t_ff_1_q);
  and and_10 (and_10_out, t_ff_3_q, not_3_out, not_4_out);
  and and_11 (and_11_out, t_ff_2_q, t_ff_1_q);
  and and_12 (and_12_out, t_ff_4_q, not_3_out, not_4_out);
  and and_13 (and_13_out, not_1_out, not_2_out, t_ff_1_q);
  and and_14 (and_14_out, not_1_out, not_3_out, t_ff_1_q);
  and and_15 (and_15_out, t_ff_3_q, t_ff_2_q, not_4_out);
  and and_16 (and_16_out, t_ff_4_q, not_4_out);
  not not_5 (not_5_out, t_ff_2_q);
  not not_6 (not_6_out, t_ff_4_q);
  T_Flip_Flop t_ff_4 (.T(en), .clk(t_ff_3_q), .Q(t_ff_4_q), .reset(or_5_out));  // open: Qn, preset
  or or_2 (out_4[2], and_4_out, and_5_out, and_6_out, and_7_out, and_8_out);
  or or_3 (out_4[1], and_9_out, and_10_out, and_11_out, and_12_out);
  or or_4 (out_4[0], and_13_out, and_14_out, and_15_out, and_16_out);
  and and_17 (and_17_out, t_ff_1_q, not_5_out, t_ff_3_q, not_6_out);
  or or_5 (or_5_out, and_17_out, reset);
endmodule

module just_one_decoder (
  input  reset,
  input  en,
  input  CLK,
  output [3:0] Output_bus_1
);

  wire and_1_out, decoder_1_out1, decoder_1_out2, decoder_1_out3, decoder_1_out4, decoder_1_out5,
       decoder_1_out6, decoder_1_out7, decoder_1_out8, decoder_1_out9, decoder_1_out10, decoder_1_out11,
       decoder_1_out12, decoder_1_out13, decoder_1_out14, decoder_1_out15, not_1_out, not_2_out, or_1_out;
  wire [3:0] t_ff_1_q;

  T_Flip_Flop t_ff_1 (.T(en), .clk(CLK), .Q(t_ff_1_q[0]), .reset(or_1_out));  // open: Qn, preset
  T_Flip_Flop t_ff_2 (.T(en), .clk(t_ff_1_q[0]), .Q(t_ff_1_q[1]), .reset(or_1_out));  // open: Qn, preset
  T_Flip_Flop t_ff_3 (.T(en), .clk(t_ff_1_q[1]), .Q(t_ff_1_q[2]), .reset(or_1_out));  // open: Qn, preset
  Decoder #(.select(4)) decoder_1 (
    .out1(decoder_1_out1), .out2(decoder_1_out2), .out3(decoder_1_out3), .out4(decoder_1_out4),
    .out5(decoder_1_out5), .out6(decoder_1_out6), .out7(decoder_1_out7), .out8(decoder_1_out8),
    .out9(decoder_1_out9), .out10(decoder_1_out10), .out11(decoder_1_out11), .out12(decoder_1_out12),
    .out13(decoder_1_out13), .out14(decoder_1_out14), .out15(decoder_1_out15), .sel(t_ff_1_q));  // open: out0, en
  not not_1 (not_1_out, t_ff_1_q[1]);
  not not_2 (not_2_out, t_ff_1_q[3]);
  T_Flip_Flop t_ff_4 (.T(en), .clk(t_ff_1_q[2]), .Q(t_ff_1_q[3]), .reset(or_1_out));  // open: Qn, preset
  and and_1 (and_1_out, t_ff_1_q[0], not_1_out, t_ff_1_q[2], not_2_out);
  or or_1 (or_1_out, and_1_out, reset);
  or or_2 (Output_bus_1[3], decoder_1_out2, decoder_1_out13, decoder_1_out14, decoder_1_out15);
  or or_3 (Output_bus_1[2], decoder_1_out5, decoder_1_out4, decoder_1_out3, decoder_1_out9, decoder_1_out10, decoder_1_out11, decoder_1_out12);
  or or_4 (Output_bus_1[1], decoder_1_out1, decoder_1_out3, decoder_1_out5, decoder_1_out7, decoder_1_out8, decoder_1_out11, decoder_1_out12, decoder_1_out15);
  or or_5 (Output_bus_1[0], decoder_1_out1, decoder_1_out3, decoder_1_out5, decoder_1_out6, decoder_1_out8, decoder_1_out10, decoder_1_out12, decoder_1_out14);
endmodule

module counter_just_with_decoders (
  input  reset,
  input  en,
  input  CLK,
  output [3:0] out_4
);

  wire and_1_out, decoder_1_out3, decoder_1_out4, decoder_1_out5, decoder_1_out9, decoder_1_out10,
       decoder_1_out11, decoder_1_out12, decoder_2_out2, decoder_2_out13, decoder_2_out14, decoder_2_out15,
       decoder_3_out1, decoder_3_out3, decoder_3_out5, decoder_3_out7, decoder_3_out8, decoder_3_out11,
       decoder_3_out12, decoder_3_out15, decoder_4_out1, decoder_4_out3, decoder_4_out5, decoder_4_out6,
       decoder_4_out8, decoder_4_out10, decoder_4_out12, decoder_4_out14, not_1_out, not_2_out, not_3_out,
       or_5_out;
  wire [3:0] t_ff_1_q;

  T_Flip_Flop t_ff_1 (.T(en), .clk(CLK), .Q(t_ff_1_q[0]), .reset(or_5_out));  // open: Qn, preset
  Decoder #(.select(4)) decoder_1 (
    .out3(decoder_1_out3), .out4(decoder_1_out4), .out5(decoder_1_out5), .out9(decoder_1_out9),
    .out10(decoder_1_out10), .out11(decoder_1_out11), .out12(decoder_1_out12), .sel(t_ff_1_q));  // open: out0, out1, out2, out6, out7, out8, out13, out14, out15, en
  T_Flip_Flop t_ff_2 (.T(en), .clk(t_ff_1_q[0]), .Q(t_ff_1_q[1]), .reset(or_5_out));  // open: Qn, preset
  Decoder #(.select(4)) decoder_2 (
    .out2(decoder_2_out2), .out13(decoder_2_out13), .out14(decoder_2_out14), .out15(decoder_2_out15),
    .sel(t_ff_1_q));  // open: out0, out1, out3, out4, out5, out6, out7, out8, out9, out10, out11, out12, en
  Decoder #(.select(4)) decoder_3 (
    .out1(decoder_3_out1), .out3(decoder_3_out3), .out5(decoder_3_out5), .out7(decoder_3_out7),
    .out8(decoder_3_out8), .out11(decoder_3_out11), .out12(decoder_3_out12), .out15(decoder_3_out15),
    .sel(t_ff_1_q));  // open: out0, out2, out4, out6, out9, out10, out13, out14, en
  Decoder #(.select(4)) decoder_4 (
    .out1(decoder_4_out1), .out3(decoder_4_out3), .out5(decoder_4_out5), .out6(decoder_4_out6),
    .out8(decoder_4_out8), .out10(decoder_4_out10), .out12(decoder_4_out12), .out14(decoder_4_out14),
    .sel(t_ff_1_q));  // open: out0, out2, out4, out7, out9, out11, out13, out15, en
  T_Flip_Flop t_ff_3 (.T(en), .clk(t_ff_1_q[1]), .Q(t_ff_1_q[2]), .reset(or_5_out));  // open: Qn, preset
  or or_1 (out_4[3], decoder_2_out2, decoder_2_out13, decoder_2_out14, decoder_2_out15);
  or or_2 (out_4[2], decoder_1_out3, decoder_1_out4, decoder_1_out5, decoder_1_out9, decoder_1_out10, decoder_1_out11, decoder_1_out12);
  or or_3 (out_4[1], decoder_3_out1, decoder_3_out3, decoder_3_out5, decoder_3_out7, decoder_3_out8, decoder_3_out11, decoder_3_out12, decoder_3_out15);
  not not_1 (not_1_out, t_ff_1_q[0]);
  not not_2 (not_2_out, t_ff_1_q[1]);
  not not_3 (not_3_out, t_ff_1_q[3]);
  T_Flip_Flop t_ff_4 (.T(en), .clk(t_ff_1_q[2]), .Q(t_ff_1_q[3]), .reset(or_5_out));  // open: Qn, preset
  or or_4 (out_4[0], decoder_4_out1, decoder_4_out3, decoder_4_out5, decoder_4_out6, decoder_4_out8, decoder_4_out10, decoder_4_out12, decoder_4_out14);
  and and_1 (and_1_out, not_1_out, not_2_out, t_ff_1_q[2], not_3_out);
  or or_5 (or_5_out, and_1_out, reset);
endmodule
