// Logisim project Final_lab.circ as structural Verilog: 16 circuits, main circuit main
module main (
  input  en_t,
  input  en_p
);

  wire and_1_out, and_2_out, and_3_out, and_4_out, and_5_out, and_6_out, clk, Green_1, Green_2, lights,
       not_1_out, not_2_out, off_2, one, or_2_out, or_4_out, Red_1, Red_2, two, Yellow_1, Yellow_2;
  wire [7:0] HEX_0, HEX_0_1, HEX_0_2, HEX_0_5, HEX_0_6, HEX_1, HEX_1_1, HEX_1_2, lights_8, off_8, or_1_out,
       or_3_out;

  and and_1 (and_1_out, Red_2, ~one);  // AND_Gate
  _7_Segment_Display #(.active("false")) L_7_Segment_Display_1 (
    .g(or_1_out[6]), .f(or_1_out[5]), .a(or_1_out[0]), .b(or_1_out[1]), .e(or_1_out[4]), .d(or_1_out[3]),
    .c(or_1_out[2]), .dp(or_1_out[7]));
  assign or_1_out = HEX_1_1 | HEX_1;  // OR_Gate or_1, 8 bits wide
  or or_2 (or_2_out, ~lights, Red_1);  // OR_Gate
  and and_2 (and_2_out, Yellow_1, lights);
  and and_3 (and_3_out, Green_1, lights);
  _7_Segment_Display #(.active("false")) L_7_Segment_Display_2 (
    .g(HEX_0_6[6]), .f(HEX_0_6[5]), .a(HEX_0_6[0]), .b(HEX_0_6[1]), .e(HEX_0_6[4]), .d(HEX_0_6[3]),
    .c(HEX_0_6[2]), .dp(HEX_0_6[7]));
  not not_1 (not_1_out, lights);
  // RGBLED RGBLED_4: pin names not known; wires that end beside it: or_2_out
  // RGBLED RGBLED_5: pin names not known; wires that end beside it: and_2_out, and_2_out
  // RGBLED RGBLED_6: pin names not known; wires that end beside it: and_3_out
  FSM_with_Display FSM_with_Display_1 (
    .en(en_t), .red_2(and_1_out), .off(off_2), .CLK(clk), .clear(not_1_out), .Green(Green_1),
    .HEX_1(HEX_1_1), .Yellow(Yellow_1), .red(Red_1), .HEX_0(HEX_0_1));
  Clock clock_1 (.out(clk));
  two_way_walkway_with_countdown two_way_walkway_with_countdown_1 (
    .HEX_0_2(HEX_0_2), .HEX_0_0(HEX_0_1), .red_1(Red_1), .en_p(en_p), .red_2(Red_2), .clk(clk),
    .HEX_0(HEX_0), .HEX_1(HEX_1), .one(one), .off_8(off_8), .two(two), .off_2(off_2), .lights_8(lights_8),
    .lights(lights));
  and and_4 (and_4_out, Red_1, ~two);  // AND_Gate
  _7_Segment_Display #(.active("false")) L_7_Segment_Display_3 (
    .g(or_3_out[6]), .f(or_3_out[5]), .a(or_3_out[0]), .b(or_3_out[1]), .e(or_3_out[4]), .d(or_3_out[3]),
    .c(or_3_out[2]), .dp(or_3_out[7]));
  assign or_3_out = HEX_1_2 | HEX_1;  // OR_Gate or_3, 8 bits wide
  not not_2 (not_2_out, lights);
  or or_4 (or_4_out, Red_2, ~lights);  // OR_Gate
  // RGBLED RGBLED_1: pin names not known; wires that end beside it: or_4_out
  and and_5 (and_5_out, lights, Yellow_2);
  // RGBLED RGBLED_2: pin names not known; wires that end beside it: and_5_out, and_5_out
  and and_6 (and_6_out, lights, Green_2);
  // RGBLED RGBLED_3: pin names not known; wires that end beside it: and_6_out
  _7_Segment_Display #(.active("false")) L_7_Segment_Display_4 (
    .g(HEX_0_5[6]), .f(HEX_0_5[5]), .a(HEX_0_5[0]), .b(HEX_0_5[1]), .e(HEX_0_5[4]), .d(HEX_0_5[3]),
    .c(HEX_0_5[2]), .dp(HEX_0_5[7]));
  FSM_2_with_display FSM_2_with_display_1 (
    .en_t(en_t), .red_1(and_4_out), .off(off_2), .CLK(clk), .clear(not_2_out), .G(Green_2), .HEX_1(HEX_1_2),
    .Y(Yellow_2), .R(Red_2), .HEX_0(HEX_0_2));
  display display_1 (.HEX_0_0(HEX_0_1), .off_8bit(off_8), .HEX_0_1(HEX_0), .Hex_0(HEX_0_6));
  display display_2 (.HEX_0_0(HEX_0_2), .off_8bit(off_8), .HEX_0_1(HEX_0), .Hex_0(HEX_0_5));

  // Notes on the sheet:
  //   Counter Display
  //   Counter Display
endmodule

module DownCounter (
  input  en,
  input  clk,
  output [3:0] count
);

  wire and_1_out, and_2_out, and_3_out, and_4_out, or_1_out, or_2_out, t_ff_1_q, t_ff_2_q, t_ff_3_q;

  or or_1 (or_1_out, count[0], count[1], count[2], count[3]);
  or or_2 (or_2_out, or_1_out, en);
  T_Flip_Flop t_ff_1 (.T(or_2_out), .clk(clk), .Q(t_ff_1_q), .Qn(count[0]), .preset(and_1_out));  // open: reset
  and and_1 (and_1_out, count[0], count[1], count[2], count[3]);
  and and_2 (and_2_out, or_2_out, t_ff_1_q);
  T_Flip_Flop t_ff_2 (.T(and_2_out), .clk(clk), .Q(t_ff_2_q), .Qn(count[1]));  // open: reset, preset
  and and_3 (and_3_out, and_2_out, t_ff_2_q);
  T_Flip_Flop t_ff_3 (.T(and_3_out), .clk(clk), .Q(t_ff_3_q), .Qn(count[2]), .preset(and_1_out));  // open: reset
  and and_4 (and_4_out, and_3_out, t_ff_3_q);
  T_Flip_Flop t_ff_4 (.T(and_4_out), .clk(clk), .Qn(count[3]));  // open: Q, reset, preset

  // Notes on the sheet:
  //   Synchronous Down Counter from 10 to 0 with reset
endmodule

module FSM_2 (
  input  en,
  input  next_state,
  input  clear,
  output G,
  output Y,
  output R,
  output rst
);

  wire [1:0] multiplexer_1_out, register_1_q;

  Multiplexer #(.select(3), .width(2)) multiplexer_1 (
    .in0(2'b00), .in1(2'b01), .in2(2'b10), .in4(2'b01), .in5(2'b10), .in6(2'b00), .out(multiplexer_1_out),
    .sel({en, register_1_q}));  // open: in3, in7
  // Probe on multiplexer_1_out
  Register #(.width(2)) register_1 (
    .D(multiplexer_1_out), .Q(register_1_q), .clk(next_state), .clr(clear));  // open: en
  // Probe on register_1_q
  and and_1 (G, register_1_q[0], ~register_1_q[1]);  // AND_Gate
  and and_2 (Y, ~register_1_q[0], register_1_q[1]);  // AND_Gate
  and and_3 (R, ~register_1_q[0], ~register_1_q[1]);  // AND_Gate

  assign rst = next_state;
endmodule

module something (
  input  en,
  input  Input_1
);

  wire and_1_out, and_2_out, and_3_out, and_4_out, clk, G, G_2, nState, nState_2, or_1_out, or_2_out,
       pedestrian_button_1_en, pedestrian_button_2_en, R, R_2, Y, Y_2;
  wire [3:0] DownCounter_v1_1_count, DownCounter_v1_2_count;
  wire [7:0] HEX0, HEX1, HEX2, HEX3;

  and and_1 (and_1_out, en, and_2_out);
  and and_2 (and_2_out, ~DownCounter_v1_1_count[0], ~DownCounter_v1_1_count[1], ~DownCounter_v1_1_count[2], ~DownCounter_v1_1_count[3], R_2);  // AND_Gate
  Clock u_clk (.out(clk));
  or or_1 (or_1_out, nState, pedestrian_button_1_en);
  and and_3 (and_3_out, ~DownCounter_v1_2_count[0], ~DownCounter_v1_2_count[1], ~DownCounter_v1_2_count[2], ~DownCounter_v1_2_count[3], R);  // AND_Gate
  Clock clock_1 (.out(clk));
  or or_2 (or_2_out, nState_2, pedestrian_button_2_en);
  // RGBLED RGBLED_1: pin names not known; wires that end beside it: R
  // RGBLED RGBLED_2: pin names not known; wires that end beside it: Y, Y
  // RGBLED RGBLED_3: pin names not known; wires that end beside it: G
  and and_4 (and_4_out, Input_1, and_3_out);
  FSM FSM_1 (.en(en), .next_state(and_1_out), .G(G), .Y(Y), .R(R), .rst(nState));  // open: clear
  // RGBLED RGBLED_4: pin names not known; wires that end beside it: R_2
  // RGBLED RGBLED_5: pin names not known; wires that end beside it: Y_2, Y_2
  // RGBLED RGBLED_6: pin names not known; wires that end beside it: G_2
  DownCounter_v1 DownCounter_v1_1 (.en(or_1_out), .clk(clk), .count(DownCounter_v1_1_count));
  pedestrian_button pedestrian_button_1 (.counter(DownCounter_v1_1_count), .en(pedestrian_button_1_en));
  FSM_2 FSM_2_1 (.en(Input_1), .next_state(and_4_out), .G(G_2), .Y(Y_2), .R(R_2), .rst(nState_2));  // open: clear
  _7_Segment_Display #(.active("false")) L_7_Segment_Display_1 (
    .g(HEX1[6]), .f(HEX1[5]), .a(HEX1[0]), .b(HEX1[1]), .e(HEX1[4]), .d(HEX1[3]), .c(HEX1[2]), .dp(HEX1[7]));
  DownCounter_v1 DownCounter_v1_2 (.en(or_2_out), .clk(clk), .count(DownCounter_v1_2_count));
  _7_Segment_Display #(.active("false")) L_7_Segment_Display_2 (
    .g(HEX0[6]), .f(HEX0[5]), .a(HEX0[0]), .b(HEX0[1]), .e(HEX0[4]), .d(HEX0[3]), .c(HEX0[2]), .dp(HEX0[7]));
  _7_Segment_Display #(.active("false")) L_7_Segment_Display_3 (
    .g(HEX3[6]), .f(HEX3[5]), .a(HEX3[0]), .b(HEX3[1]), .e(HEX3[4]), .d(HEX3[3]), .c(HEX3[2]), .dp(HEX3[7]));
  pedestrian_button pedestrian_button_2 (.counter(DownCounter_v1_2_count), .en(pedestrian_button_2_en));
  _7_Segment_Display #(.active("false")) L_7_Segment_Display_4 (
    .g(HEX2[6]), .f(HEX2[5]), .a(HEX2[0]), .b(HEX2[1]), .e(HEX2[4]), .d(HEX2[3]), .c(HEX2[2]), .dp(HEX2[7]));
  Bin2Hex Bin2Hex_1 (
    .v3(DownCounter_v1_1_count[3]), .v2(DownCounter_v1_1_count[2]), .v1(DownCounter_v1_1_count[1]),
    .v0(DownCounter_v1_1_count[0]), .HEX1(HEX1), .HEX0(HEX0));
  Bin2Hex Bin2Hex_2 (
    .v3(DownCounter_v1_2_count[3]), .v2(DownCounter_v1_2_count[2]), .v1(DownCounter_v1_2_count[1]),
    .v0(DownCounter_v1_2_count[0]), .HEX1(HEX3), .HEX0(HEX2));

  // Notes on the sheet:
  //   Traffic Light A
  //   Traffic Light B
  //   Counter Display
  //   Counter Display
endmodule

module countdown_with_display (
  input  en,
  input  clk,
  output [7:0] HEX0,
  output [7:0] HEX1,
  output off
);

  wire [3:0] DownCounter_1_count;

  DownCounter DownCounter_1 (.en(en), .clk(clk), .count(DownCounter_1_count));
  and and_1 (off, ~DownCounter_1_count[3], ~DownCounter_1_count[2], ~DownCounter_1_count[1], ~DownCounter_1_count[0]);  // AND_Gate
  _7_Segment_Display #(.active("false")) L_7_Segment_Display_3 (
    .g(HEX1[6]), .f(HEX1[5]), .a(HEX1[0]), .b(HEX1[1]), .e(HEX1[4]), .d(HEX1[3]), .c(HEX1[2]), .dp(HEX1[7]));
  _7_Segment_Display #(.active("false")) L_7_Segment_Display_4 (
    .g(HEX0[6]), .f(HEX0[5]), .a(HEX0[0]), .b(HEX0[1]), .e(HEX0[4]), .d(HEX0[3]), .c(HEX0[2]), .dp(HEX0[7]));
  Bin2Hex Bin2Hex_1 (
    .v3(DownCounter_1_count[3]), .v2(DownCounter_1_count[2]), .v1(DownCounter_1_count[1]),
    .v0(DownCounter_1_count[0]), .HEX1(HEX1), .HEX0(HEX0));

  // Notes on the sheet:
  //   Counter Display
endmodule

module countdown_with_one_FSM (
  input  red_2,
  input  en_t,
  input  clk,
  input  en_p,
  output red_1,
  output yellow,
  output green,
  output [7:0] HEX_0,
  output [7:0] HEX_1
);

  wire fsm_with_display_1_green, fsm_with_display_1_red, fsm_with_display_1_yellow, not_1_out, walkway_1_en;
  wire [7:0] countdown_with_display_1_hex0, countdown_with_display_1_hex1, fsm_with_display_1_hex_0,
       fsm_with_display_1_hex_1;
  wire [7:7] off_8_bit;

  not not_1 (not_1_out, off_8_bit[7]);
  and and_1 (yellow, off_8_bit[7], fsm_with_display_1_yellow);
  or or_1 (red_1, not_1_out, fsm_with_display_1_red);
  walkway walkway_1 (.off(off_8_bit[7]), .red_1or2(fsm_with_display_1_red), .en_p(en_p), .clk(clk), .en(walkway_1_en));
  // RGBLED rgbled_1: pin names not known; wires that end beside it: red_1
  // RGBLED rgbled_2: pin names not known; wires that end beside it: yellow, yellow
  and and_2 (green, fsm_with_display_1_green, off_8_bit[7]);
  // RGBLED rgbled_3: pin names not known; wires that end beside it: green
  FSM_with_Display fsm_with_display_1 (
    .en(en_t), .red_2(off_8_bit[7]), .off(red_2), .CLK(clk), .Green(fsm_with_display_1_green),
    .HEX_1(fsm_with_display_1_hex_1), .Yellow(fsm_with_display_1_yellow), .red(fsm_with_display_1_red),
    .HEX_0(fsm_with_display_1_hex_0));  // open: clear
  countdown_with_display countdown_with_display_1 (
    .en(walkway_1_en), .clk(clk), .HEX0(countdown_with_display_1_hex0), .HEX1(countdown_with_display_1_hex1),
    .off(off_8_bit[7]));
  _7_Segment_Display #(.active("false")) L_7_Segment_Display_3 (
    .g(HEX_1[6]), .f(HEX_1[5]), .a(HEX_1[0]), .b(HEX_1[1]), .e(HEX_1[4]), .d(HEX_1[3]), .c(HEX_1[2]),
    .dp(HEX_1[7]));
  assign HEX_1 = fsm_with_display_1_hex_1 | countdown_with_display_1_hex1;  // OR_Gate or_2, 8 bits wide
  _7_Segment_Display #(.active("false")) L_7_Segment_Display_4 (
    .g(HEX_0[6]), .f(HEX_0[5]), .a(HEX_0[0]), .b(HEX_0[1]), .e(HEX_0[4]), .d(HEX_0[3]), .c(HEX_0[2]),
    .dp(HEX_0[7]));
  display display_1 (
    .HEX_0_0(fsm_with_display_1_hex_0), .off_8bit({8{off_8_bit[7]}}),
    .HEX_0_1(countdown_with_display_1_hex0), .Hex_0(HEX_0));

  // Other names for the same wires on the sheet: off_8_bit[6:0] = {7{off_8_bit[7]}}
endmodule

module FSM_with_Display (
  input  en,
  input  red_2,
  input  off,
  input  CLK,
  input  clear,
  output Green,
  output [7:0] HEX_1,
  output Yellow,
  output red,
  output [7:0] HEX_0
);

  wire and_1_out, and_2_out, FSM_1_rst, or_1_out, pedestrian_button_1_en;
  wire [3:0] DownCounter_v1_1_count;

  and and_1 (and_1_out, ~DownCounter_v1_1_count[0], ~DownCounter_v1_1_count[1], ~DownCounter_v1_1_count[2], ~DownCounter_v1_1_count[3], red_2, off);  // AND_Gate
  and and_2 (and_2_out, en, and_1_out);
  or or_1 (or_1_out, FSM_1_rst, pedestrian_button_1_en);
  // RGBLED RGBLED_1: pin names not known; wires that end beside it: red
  // RGBLED RGBLED_2: pin names not known; wires that end beside it: Yellow, Yellow
  // RGBLED RGBLED_3: pin names not known; wires that end beside it: Green
  FSM FSM_1 (.en(en), .clear(clear), .next_state(and_2_out), .G(Green), .Y(Yellow), .R(red), .rst(FSM_1_rst));
  DownCounter_v1 DownCounter_v1_1 (.en(or_1_out), .clk(CLK), .count(DownCounter_v1_1_count));
  pedestrian_button pedestrian_button_1 (.counter(DownCounter_v1_1_count), .en(pedestrian_button_1_en));
  _7_Segment_Display #(.active("false")) L_7_Segment_Display_1 (
    .g(HEX_1[6]), .f(HEX_1[5]), .a(HEX_1[0]), .b(HEX_1[1]), .e(HEX_1[4]), .d(HEX_1[3]), .c(HEX_1[2]),
    .dp(HEX_1[7]));
  _7_Segment_Display #(.active("false")) L_7_Segment_Display_2 (
    .g(HEX_0[6]), .f(HEX_0[5]), .a(HEX_0[0]), .b(HEX_0[1]), .e(HEX_0[4]), .d(HEX_0[3]), .c(HEX_0[2]),
    .dp(HEX_0[7]));
  Bin2Hex Bin2Hex_1 (
    .v3(DownCounter_v1_1_count[3]), .v2(DownCounter_v1_1_count[2]), .v1(DownCounter_v1_1_count[1]),
    .v0(DownCounter_v1_1_count[0]), .HEX1(HEX_1), .HEX0(HEX_0));

  // Other names for the same wires on the sheet: G = Green; HEX0[7:0] = HEX_0; HEX1[7:0] = HEX_1; R = red; Y = Yellow

  // Notes on the sheet:
  //   Traffic Light A
  //   Counter Display
endmodule

module FSM_2_with_display (
  input  en_t,
  input  red_1,
  input  off,
  input  CLK,
  input  clear,
  output G,
  output [7:0] HEX_1,
  output Y,
  output R,
  output [7:0] HEX_0
);

  wire and_1_out, and_2_out, clk_t, FSM_2_1_rst, or_1_out, pedestrian_button_2_en;
  wire [3:0] DownCounter_v1_2_count;

  and and_1 (and_1_out, ~DownCounter_v1_2_count[0], ~DownCounter_v1_2_count[1], ~DownCounter_v1_2_count[2], ~DownCounter_v1_2_count[3], red_1, off);  // AND_Gate
  Clock clock_1 (.out(clk_t));
  or or_1 (or_1_out, FSM_2_1_rst, pedestrian_button_2_en);
  and and_2 (and_2_out, en_t, and_1_out);
  // RGBLED RGBLED_4: pin names not known; wires that end beside it: R
  // RGBLED RGBLED_5: pin names not known; wires that end beside it: Y, Y
  // RGBLED RGBLED_6: pin names not known; wires that end beside it: G
  FSM_2 FSM_2_1 (.en(en_t), .next_state(and_2_out), .clear(clear), .G(G), .Y(Y), .R(R), .rst(FSM_2_1_rst));
  DownCounter_v1 DownCounter_v1_2 (.en(or_1_out), .clk(CLK), .count(DownCounter_v1_2_count));
  _7_Segment_Display #(.active("false")) L_7_Segment_Display_3 (
    .g(HEX_1[6]), .f(HEX_1[5]), .a(HEX_1[0]), .b(HEX_1[1]), .e(HEX_1[4]), .d(HEX_1[3]), .c(HEX_1[2]),
    .dp(HEX_1[7]));
  pedestrian_button pedestrian_button_2 (.counter(DownCounter_v1_2_count), .en(pedestrian_button_2_en));
  _7_Segment_Display #(.active("false")) L_7_Segment_Display_4 (
    .g(HEX_0[6]), .f(HEX_0[5]), .a(HEX_0[0]), .b(HEX_0[1]), .e(HEX_0[4]), .d(HEX_0[3]), .c(HEX_0[2]),
    .dp(HEX_0[7]));
  Bin2Hex Bin2Hex_2 (
    .v3(DownCounter_v1_2_count[3]), .v2(DownCounter_v1_2_count[2]), .v1(DownCounter_v1_2_count[1]),
    .v0(DownCounter_v1_2_count[0]), .HEX1(HEX_1), .HEX0(HEX_0));

  // Other names for the same wires on the sheet: G_2 = G; HEX2[7:0] = HEX_0; HEX3[7:0] = HEX_1; R_2 = R; Y_2 = Y

  // Notes on the sheet:
  //   Traffic Light B
  //   Counter Display
endmodule

module countdown_with_FSM_2 (
  input  red_1,
  input  en_t,
  input  en_p,
  output red_2,
  output yellow,
  output green,
  output [7:0] HEX_1,
  output [7:0] HEX_0
);

  wire clock_1_out, fsm_2_with_display_1_g, fsm_2_with_display_1_r, fsm_2_with_display_1_y, not_1_out,
       walkway_1_en;
  wire [7:0] countdown_with_display_1_hex0, countdown_with_display_1_hex1, fsm_2_with_display_1_hex_0,
       fsm_2_with_display_1_hex_1;
  wire [7:7] off_8_bit;

  not not_1 (not_1_out, off_8_bit[7]);
  or or_1 (red_2, not_1_out, fsm_2_with_display_1_r);
  and and_1 (yellow, off_8_bit[7], fsm_2_with_display_1_y);
  Clock clock_1 (.out(clock_1_out));
  // RGBLED rgbled_1: pin names not known; wires that end beside it: red_2
  walkway walkway_1 (
    .off(off_8_bit[7]), .red_1or2(fsm_2_with_display_1_r), .en_p(en_p), .clk(clock_1_out), .en(walkway_1_en));
  // RGBLED rgbled_2: pin names not known; wires that end beside it: yellow, yellow
  and and_2 (green, fsm_2_with_display_1_g, off_8_bit[7]);
  // RGBLED rgbled_3: pin names not known; wires that end beside it: green
  FSM_2_with_display fsm_2_with_display_1 (
    .en_t(en_t), .red_1(red_1), .off(off_8_bit[7]), .CLK(clock_1_out), .G(fsm_2_with_display_1_g),
    .HEX_1(fsm_2_with_display_1_hex_1), .Y(fsm_2_with_display_1_y), .R(fsm_2_with_display_1_r),
    .HEX_0(fsm_2_with_display_1_hex_0));  // open: clear
  countdown_with_display countdown_with_display_1 (
    .en(walkway_1_en), .clk(clock_1_out), .HEX0(countdown_with_display_1_hex0),
    .HEX1(countdown_with_display_1_hex1), .off(off_8_bit[7]));
  _7_Segment_Display #(.active("false")) L_7_Segment_Display_3 (
    .g(HEX_1[6]), .f(HEX_1[5]), .a(HEX_1[0]), .b(HEX_1[1]), .e(HEX_1[4]), .d(HEX_1[3]), .c(HEX_1[2]),
    .dp(HEX_1[7]));
  assign HEX_1 = fsm_2_with_display_1_hex_1 | countdown_with_display_1_hex1;  // OR_Gate or_2, 8 bits wide
  _7_Segment_Display #(.active("false")) L_7_Segment_Display_4 (
    .g(HEX_0[6]), .f(HEX_0[5]), .a(HEX_0[0]), .b(HEX_0[1]), .e(HEX_0[4]), .d(HEX_0[3]), .c(HEX_0[2]),
    .dp(HEX_0[7]));
  display display_1 (
    .HEX_0_0(fsm_2_with_display_1_hex_0), .off_8bit({8{off_8_bit[7]}}),
    .HEX_0_1(countdown_with_display_1_hex0), .Hex_0(HEX_0));

  // Other names for the same wires on the sheet: off_8_bit[6:0] = {7{off_8_bit[7]}}
endmodule

module walkway (
  input  off,
  input  red_1or2,
  input  en_p,
  input  clk,
  output en
);

  wire and_1_out, or_1_out, register_1_q;

  or or_1 (or_1_out, register_1_q, en_p);
  and and_1 (and_1_out, off, or_1_out);
  Register #(.width(1)) register_1 (.D(and_1_out), .Q(register_1_q), .clk(clk));  // open: en, clr
  and and_2 (en, red_1or2, register_1_q);
endmodule

module display (
  input  [7:0] HEX_0_0,
  input  [7:0] off_8bit,
  input  [7:0] HEX_0_1,
  output [7:0] Hex_0
);

  wire [7:0] and_1_out, and_2_out;

  assign and_1_out = HEX_0_0 & off_8bit;  // AND_Gate and_1, 8 bits wide
  assign Hex_0 = and_1_out | and_2_out;  // OR_Gate or_1, 8 bits wide
  assign and_2_out = HEX_0_1 & ~off_8bit;  // AND_Gate and_2, 8 bits wide
endmodule

module walkway_with_countdown (
  input  red_1,
  input  en_p,
  input  clk,
  output [7:0] HEX_0,
  output [7:0] HEX_1,
  output off,
  output [7:0] off_8bit
);

  wire walkway_1_en;

  walkway walkway_1 (.off(off), .red_1or2(red_1), .en_p(en_p), .clk(clk), .en(walkway_1_en));
  countdown_with_display countdown_with_display_1 (.en(walkway_1_en), .clk(clk), .HEX0(HEX_0), .HEX1(HEX_1), .off(off));

  assign off_8bit = {8{off}};
endmodule

module leds (
  input  g,
  input  y,
  input  r,
  input  off,
  output red,
  output yellow,
  output green
);

  wire not_1_out;

  not not_1 (not_1_out, off);
  or or_1 (red, not_1_out, r);
  and and_1 (yellow, off, y);
  and and_2 (green, off, g);
endmodule

module countdown_with_FSM_less_wires (
  input  red_1,
  input  en_t,
  input  en_p,
  input  clk,
  output [7:0] HEX_1,
  output [7:0] HEX_0,
  output green_2,
  output yellow_2,
  output red_2
);

  wire clk_t, clock_1_out, green_2_t, off, red_1_t, red_2_t, yellow_2_t;
  wire [7:0] fsm_2_with_display_1_hex_0, fsm_2_with_display_1_hex_1, off_8_bit,
       walkway_with_countdown_1_hex_0, walkway_with_countdown_1_hex_1;

  buf buffer_1 (red_1_t, red_1);
  Clock clock_1 (.out(clock_1_out));
  leds leds_1 (.g(green_2_t), .y(yellow_2_t), .r(red_2_t), .off(off), .red(red_2), .yellow(yellow_2), .green(green_2));
  or or_1 (clk_t, clock_1_out, clk);
  // RGBLED rgbled_1: pin names not known; wires that end beside it: red_2
  // RGBLED rgbled_2: pin names not known; wires that end beside it: yellow_2, yellow_2
  // RGBLED rgbled_3: pin names not known; wires that end beside it: green_2
  FSM_2_with_display fsm_2_with_display_1 (
    .en_t(en_t), .red_1(red_1_t), .off(off), .CLK(clk_t), .G(green_2_t), .HEX_1(fsm_2_with_display_1_hex_1),
    .Y(yellow_2_t), .R(red_2_t), .HEX_0(fsm_2_with_display_1_hex_0));  // open: clear
  walkway_with_countdown walkway_with_countdown_1 (
    .red_1(red_1_t), .en_p(red_2_t), .clk(en_p), .HEX_0(walkway_with_countdown_1_hex_0),
    .HEX_1(walkway_with_countdown_1_hex_1), .off(off), .off_8bit(off_8_bit));
  // Probe on fsm_2_with_display_1_hex_0
  _7_Segment_Display #(.active("false")) L_7_Segment_Display_3 (
    .g(HEX_1[6]), .f(HEX_1[5]), .a(HEX_1[0]), .b(HEX_1[1]), .e(HEX_1[4]), .d(HEX_1[3]), .c(HEX_1[2]),
    .dp(HEX_1[7]));
  assign HEX_1 = fsm_2_with_display_1_hex_1 | walkway_with_countdown_1_hex_1;  // OR_Gate or_2, 8 bits wide
  _7_Segment_Display #(.active("false")) L_7_Segment_Display_4 (
    .g(HEX_0[6]), .f(HEX_0[5]), .a(HEX_0[0]), .b(HEX_0[1]), .e(HEX_0[4]), .d(HEX_0[3]), .c(HEX_0[2]),
    .dp(HEX_0[7]));
  display display_1 (
    .HEX_0_0(fsm_2_with_display_1_hex_0), .off_8bit(off_8_bit), .HEX_0_1(walkway_with_countdown_1_hex_0),
    .Hex_0(HEX_0));
endmodule

module countdown_with_FSM_lees_wires (
  input  red_2,
  input  en_t,
  input  en_p,
  input  clk,
  output [7:0] HEX_1,
  output [7:0] HEX_0,
  output green_1,
  output yello1_1,
  output red_1
);

  wire clk_t, clock_1_out, green_1_t, off, red_1_t, red_2_t, yellow_1;
  wire [7:0] fsm_with_display_1_hex_0, fsm_with_display_1_hex_1, off_8_bit, walkway_with_countdown_1_hex_0,
       walkway_with_countdown_1_hex_1;

  buf buffer_1 (red_2_t, red_2);
  Clock clock_1 (.out(clock_1_out));
  leds leds_1 (.g(green_1_t), .y(yellow_1), .r(red_1_t), .off(off), .red(red_1), .yellow(yello1_1), .green(green_1));
  or or_1 (clk_t, clock_1_out, clk);
  // RGBLED rgbled_1: pin names not known; wires that end beside it: red_1
  // RGBLED rgbled_2: pin names not known; wires that end beside it: yello1_1, yello1_1
  // RGBLED rgbled_3: pin names not known; wires that end beside it: green_1
  FSM_with_Display fsm_with_display_1 (
    .en(en_t), .red_2(red_2_t), .off(off), .CLK(clk_t), .Green(green_1_t), .HEX_1(fsm_with_display_1_hex_1),
    .Yellow(yellow_1), .red(red_1_t), .HEX_0(fsm_with_display_1_hex_0));  // open: clear
  walkway_with_countdown walkway_with_countdown_1 (
    .red_1(red_1_t), .en_p(red_2_t), .clk(en_p), .HEX_0(walkway_with_countdown_1_hex_0),
    .HEX_1(walkway_with_countdown_1_hex_1), .off(off), .off_8bit(off_8_bit));
  _7_Segment_Display #(.active("false")) L_7_Segment_Display_3 (
    .g(HEX_1[6]), .f(HEX_1[5]), .a(HEX_1[0]), .b(HEX_1[1]), .e(HEX_1[4]), .d(HEX_1[3]), .c(HEX_1[2]),
    .dp(HEX_1[7]));
  assign HEX_1 = fsm_with_display_1_hex_1 | walkway_with_countdown_1_hex_1;  // OR_Gate or_2, 8 bits wide
  _7_Segment_Display #(.active("false")) L_7_Segment_Display_4 (
    .g(HEX_0[6]), .f(HEX_0[5]), .a(HEX_0[0]), .b(HEX_0[1]), .e(HEX_0[4]), .d(HEX_0[3]), .c(HEX_0[2]),
    .dp(HEX_0[7]));
  display display_1 (
    .HEX_0_0(fsm_with_display_1_hex_0), .off_8bit(off_8_bit), .HEX_0_1(walkway_with_countdown_1_hex_0),
    .Hex_0(HEX_0));
endmodule

module two_way_walkway_with_countdown (
  input  [7:0] HEX_0_2,
  input  [7:0] HEX_0_0,
  input  red_1,
  input  en_p,
  input  red_2,
  input  clk,
  output [7:0] HEX_0,
  output [7:0] HEX_1,
  output one,
  output [7:0] off_8,
  output two,
  output off_2,
  output [7:0] lights_8,
  output lights
);

  wire and_1_out, and_2_out, clock_1_out, or_1_out;
  wire [7:0] countdown_with_display_1_hex0, display_1_hex_0, display_2_hex_0;

  walkway walkway_1 (.off(off_2), .red_1or2(red_1), .en_p(en_p), .clk(or_1_out), .en(one));
  and and_1 (and_1_out, one, two);
  walkway walkway_2 (.off(off_2), .red_1or2(red_2), .en_p(en_p), .clk(or_1_out), .en(two));
  or or_1 (or_1_out, clk, clock_1_out);
  Clock clock_1 (.out(clock_1_out));
  _7_Segment_Display #(.active("false")) L_7_Segment_Display_1 (
    .g(HEX_1[6]), .f(HEX_1[5]), .a(HEX_1[0]), .b(HEX_1[1]), .e(HEX_1[4]), .d(HEX_1[3]), .c(HEX_1[2]),
    .dp(HEX_1[7]));
  and and_2 (and_2_out, ~two, ~one, ~red_2, ~red_1);  // AND_Gate
  not not_1 (lights, and_2_out);
  _7_Segment_Display #(.active("false")) L_7_Segment_Display_2 (
    .g(HEX_0[6]), .f(HEX_0[5]), .a(HEX_0[0]), .b(HEX_0[1]), .e(HEX_0[4]), .d(HEX_0[3]), .c(HEX_0[2]),
    .dp(HEX_0[7]));
  countdown_with_display countdown_with_display_1 (
    .en(and_1_out), .clk(or_1_out), .HEX0(countdown_with_display_1_hex0), .HEX1(HEX_1), .off(off_2));
  // Probe on countdown_with_display_1_hex0
  display display_1 (
    .HEX_0_0(HEX_0_2), .off_8bit({8{off_2}}), .HEX_0_1(countdown_with_display_1_hex0), .Hex_0(display_1_hex_0));
  display display_2 (
    .HEX_0_0(HEX_0_0), .off_8bit({8{off_2}}), .HEX_0_1(countdown_with_display_1_hex0), .Hex_0(display_2_hex_0));
  assign HEX_0 = display_1_hex_0 & display_2_hex_0;  // AND_Gate and_3, 8 bits wide

  assign lights_8 = {8{lights}};
  assign off_8 = {8{off_2}};
endmodule
